# Fritzing sketch Wiring (saved by Fritzing 0.9.3b)

parts:
  S1 = H-Bridge with L298N
  Raspberry_Pi_1 = Raspberry Pi 4 [part_number=RPI-4-b]
  Part1 = Arduino Mega 2560 (Rev3)
  Right = DC Motor with two-phase hall-encoder
  Left = DC Motor with two-phase hall-encoder
  OLED1 = OLED 128x64 I2C Monochrome Display
  F1 = Fan - Ventilador [package=THT]
  GY1 = MPU-6050 Board GY-521 [form="♀ (female)" package=THT]
  Power_plug1 = USB-C plug
  USBTTL1 = Micro USB B Plug
  USBTTL2 = USB A Plug
  BAT1 = Battery Holders [package=lipo-1100mAh]
  BAT2 = Battery Holders [package=lipo-1100mAh]
  IC1 = Rasberry Pi NIOR Camera [chip_label=IC package="DIP (Dual Inline) [THT]"]  # not connected

nets:
  N1: S1.ENA, Part1.D8_PWM
  N2: S1.IN1, Part1.D9_PWM
  N3: S1.IN2, Part1.D10_PWM
  N4: S1.IN3, Part1.D11_PWM
  N5: S1.IN4, Part1.D12_PWM
  N6: S1.ENB, Part1.D13_PWM
  N7: S1.M1-01, Left.pin2
  N8: S1.M1-02, Left.pin1
  N9: S1.M2-01, Right.pin2
  N10: S1.M2-02, Right.pin1
  3V3: Raspberry_Pi_1.3v3, OLED1.VDD
  N11: Raspberry_Pi_1.GPIO2, OLED1.SDA
  N12: Raspberry_Pi_1.GPIO3, OLED1.SCK
  GND: Raspberry_Pi_1.GPIO17, Raspberry_Pi_1.GND, Raspberry_Pi_1.GPIO18, OLED1.GND, F1.GND
  5V: Raspberry_Pi_1.5V, F1.5V
  N13: Part1.A0, Power_plug1.VCC, BAT2.+
  N14: Part1.A2, BAT1.+
  N15: Part1.D21/SCL, GY1.pin3
  N16: Part1.D20/SDA, GY1.pin4, GY1.pin5
  N17: Part1.D19/RX1, Left.pin3
  N18: Part1.D18/TX1, Left.pin6
  N19: Part1.GND, Right.pin4, Left.pin4, GY1.pin2
  N20: Part1.5V, Right.pin5, Left.pin5, GY1.pin1
  N21: Part1.D2_PWM, Right.pin3
  N22: Part1.D3_PWM, Right.pin6
  N23: Power_plug1.GND, BAT2.-
  N24: USBTTL1.usb, USBTTL2.usb

custom parts:
  H-Bridge with L298N: h-bridge
  Raspberry Pi 4: The RPi4, a faster version of the awesome Raspberry Pi 2 B ARM Board with 40 pin gpio. Ready for special Raspberry Pi B+ and RPi2 Hat (Hardware attached (on) top)
  Fan - Ventilador: Ventilador de 2 pines, se encuentra comunmente en computadoras de escritorio
  MPU-6050 Board GY-521: Acelerometro y Giroscopio MPU-6050 Board GY-521
  USB-C plug: power plug
  Rasberry Pi NIOR Camera: Camera
